# Fritzing sketch protoboard_inner4 (saved by Fritzing 0.9.3b)
perfboards: 1

parts:
  Part1 = Logic Level Converter
  Part2 = Logic Level Converter
  Y1 = Resonator [frequency="16 Mhz" package=THT]  # not connected
  Y2 = Resonator [frequency="16 Mhz" package=THT]
  Y4 = Resonator [frequency="16 Mhz" package=THT]
  J6 = male pin header, 3 pins [form="♂ (male)"]
  J7 = male pin header, 3 pins [form="♂ (male)"]

nets:
  N1: Part1.TX2_LV, J7.pin3
  GND: Part1.GND, Part2.GND, Y2.GND, Y4.GND, J6.pin3
  N2: Part1.LV, J6.pin2
  N3: Part1.TX2_HV, Y4.pin_1
  N4: Part2.TX2_LV, J7.pin2
  N5: Part2.TX_LV, J7.pin1
  N6: Part2.HV, Y2.0
  N7: Part2.TX2_HV, Y2.pin_1
  N8: Y4.0, J6.pin1
